# Fritzing sketch CES_lab (saved by Fritzing 0.9.3b)
breadboards: 1

parts:
  Part1 = Arduino Uno (Rev3)
  hc-sr1 = hc-sr04
  BAT1 = Battery Holders [package=battcon_20mm]
  J1 = Piezo Speaker

nets:
  N1: Part1.D3_PWM, J1.pin2
  N2: Part1.D5_PWM, hc-sr1.Trig
  N3: Part1.D6_PWM, hc-sr1.Echo
  5V: Part1.5V, hc-sr1.VCC, BAT1.-
  GND: Part1.GND, hc-sr1.GND, J1.pin1
